// Logisim project 7 SEGMENT WITH ALL Y.circ as structural Verilog: 8 circuits, main circuit main
module main (
  input  A,
  input  B,
  input  C,
  input  D,
  input  [3:0] D_C_B_A
);

  wire y1_1_y1, y1_2_y1, y2_1_y2, y2_2_y2, y3_1_y3, y3_2_y3, y4_1_y4, y4_2_y4, y5_1_y5, y5_2_y5, y6_1_y6,
       y6_2_y6, y7_1_y7, y7_2_y7;

  Y4 y4_1 (.A(A), .B(B), .C(C), .D(D), .Y4(y4_1_y4));
  Y3 y3_1 (.A(A), .B(B), .C(C), .D(D), .Y3(y3_1_y3));
  Y2 y2_1 (.A(A), .B(B), .C(C), .D(D), .Y2(y2_1_y2));
  Y1 y1_1 (.A(A), .B(B), .C(C), .D(D), .Y1(y1_1_y1));
  _7_Segment_Display u_7_segment_display_1 (
    .g(y1_1_y1), .f(y2_1_y2), .a(y3_1_y3), .b(y4_1_y4), .e(y5_1_y5), .d(y6_1_y6), .c(y7_1_y7));  // open: dp
  Y5 y5_1 (.A(A), .B(B), .C(C), .D(D), .Y5(y5_1_y5));
  Y6 y6_1 (.A(A), .B(B), .C(C), .D(D), .Y6(y6_1_y6));
  Y7 y7_1 (.A(A), .B(B), .C(C), .D(D), .Y7(y7_1_y7));
  Y4 y4_2 (.A(D_C_B_A[0]), .B(D_C_B_A[1]), .C(D_C_B_A[2]), .D(D_C_B_A[3]), .Y4(y4_2_y4));
  Y3 y3_2 (.A(D_C_B_A[0]), .B(D_C_B_A[1]), .C(D_C_B_A[2]), .D(D_C_B_A[3]), .Y3(y3_2_y3));
  Y2 y2_2 (.A(D_C_B_A[0]), .B(D_C_B_A[1]), .C(D_C_B_A[2]), .D(D_C_B_A[3]), .Y2(y2_2_y2));
  Y1 y1_2 (.A(D_C_B_A[0]), .B(D_C_B_A[1]), .C(D_C_B_A[2]), .D(D_C_B_A[3]), .Y1(y1_2_y1));
  Y5 y5_2 (.A(D_C_B_A[0]), .B(D_C_B_A[1]), .C(D_C_B_A[2]), .D(D_C_B_A[3]), .Y5(y5_2_y5));
  Y6 y6_2 (.A(D_C_B_A[0]), .B(D_C_B_A[1]), .C(D_C_B_A[2]), .D(D_C_B_A[3]), .Y6(y6_2_y6));
  Y7 y7_2 (.A(D_C_B_A[0]), .B(D_C_B_A[1]), .C(D_C_B_A[2]), .D(D_C_B_A[3]), .Y7(y7_2_y7));
  _7_Segment_Display u_7_segment_display_2 (
    .g(y1_2_y1), .f(y2_2_y2), .a(y3_2_y3), .b(y4_2_y4), .e(y5_2_y5), .d(y6_2_y6), .c(y7_2_y7));  // open: dp
endmodule

module Y1 (
  input  A,
  input  B,
  input  C,
  input  D,
  output Y1
);

  wire and_1_out, and_2_out, and_3_out, and_4_out, and_5_out, not_1_out, not_2_out, not_3_out, not_4_out,
       not_5_out;

  not not_1 (not_1_out, B);
  and and_1 (and_1_out, not_1_out, C);
  not not_2 (not_2_out, A);
  and and_2 (and_2_out, not_2_out, B, not_3_out);
  not not_3 (not_3_out, C);
  and and_3 (and_3_out, B, not_4_out);
  not not_4 (not_4_out, D);
  and and_4 (and_4_out, A, not_5_out);
  not not_5 (not_5_out, B);
  and and_5 (and_5_out, A, C);
  or or_1 (Y1, and_1_out, and_2_out, and_3_out, and_4_out, and_5_out);
endmodule

module Y2 (
  input  A,
  input  B,
  input  C,
  input  D,
  output Y2
);

  wire and_1_out, and_2_out, and_3_out, not_1_out, not_2_out, not_3_out, not_4_out;

  not not_1 (not_1_out, C);
  and and_1 (and_1_out, not_1_out, not_2_out);
  not not_2 (not_2_out, D);
  and and_2 (and_2_out, B, not_3_out);
  not not_3 (not_3_out, C);
  and and_3 (and_3_out, B, not_4_out);
  not not_4 (not_4_out, D);
  or or_1 (Y2, and_1_out, and_2_out, and_3_out, A);
endmodule

module Y3 (
  input  A,
  input  B,
  input  C,
  input  D,
  output Y3
);

  wire and_1_out, and_2_out, not_1_out, not_2_out;

  not not_1 (not_1_out, B);
  and and_1 (and_1_out, not_1_out, not_2_out);
  not not_2 (not_2_out, D);
  and and_2 (and_2_out, B, D);
  or or_1 (Y3, and_1_out, C, and_2_out, A);
endmodule

module Y4 (
  input  A,
  input  B,
  input  C,
  input  D,
  output Y4
);

  wire and_1_out, and_2_out, and_3_out, not_1_out, not_2_out, not_3_out, not_4_out, not_5_out, not_6_out;

  not not_1 (not_1_out, A);
  not not_2 (not_2_out, C);
  and and_1 (and_1_out, not_1_out, not_2_out, not_3_out);
  not not_3 (not_3_out, D);
  not not_4 (not_4_out, B);
  not not_5 (not_5_out, A);
  and and_2 (and_2_out, not_5_out, C, D);
  not not_6 (not_6_out, C);
  and and_3 (and_3_out, A, not_6_out, D);
  or or_1 (Y4, and_1_out, not_4_out, and_2_out, and_3_out);
endmodule

module Y5 (
  input  A,
  input  B,
  input  C,
  input  D,
  output Y5
);

  wire and_1_out, and_2_out, and_3_out, and_4_out, not_1_out, not_2_out, not_3_out;

  not not_1 (not_1_out, B);
  and and_1 (and_1_out, not_1_out, not_2_out);
  not not_2 (not_2_out, D);
  and and_2 (and_2_out, C, not_3_out);
  not not_3 (not_3_out, D);
  and and_3 (and_3_out, A, C);
  and and_4 (and_4_out, A, B);
  or or_1 (Y5, and_1_out, and_2_out, and_3_out, and_4_out);
endmodule

module Y6 (
  input  A,
  input  B,
  input  C,
  input  D,
  output Y6
);

  wire and_1_out, and_2_out, and_3_out, and_4_out, and_5_out, not_1_out, not_2_out, not_3_out, not_4_out,
       not_5_out, not_6_out, not_7_out;

  not not_1 (not_1_out, A);
  not not_2 (not_2_out, B);
  and and_1 (and_1_out, not_1_out, not_2_out, not_3_out);
  not not_3 (not_3_out, D);
  not not_4 (not_4_out, B);
  and and_2 (and_2_out, not_4_out, C, D);
  not not_5 (not_5_out, C);
  and and_3 (and_3_out, B, not_5_out, D);
  and and_4 (and_4_out, B, C, not_6_out);
  not not_6 (not_6_out, D);
  and and_5 (and_5_out, A, not_7_out);
  not not_7 (not_7_out, C);
  or or_1 (Y6, and_1_out, and_2_out, and_3_out, and_4_out, and_5_out);
endmodule

module Y7 (
  input  A,
  input  B,
  input  C,
  input  D,
  output Y7
);

  wire and_1_out, and_2_out, and_3_out, and_4_out, and_5_out, not_1_out, not_2_out, not_3_out, not_4_out,
       not_5_out, not_6_out;

  not not_1 (not_1_out, A);
  and and_1 (and_1_out, not_1_out, not_2_out);
  not not_2 (not_2_out, C);
  not not_3 (not_3_out, A);
  and and_2 (and_2_out, not_3_out, D);
  not not_4 (not_4_out, C);
  and and_3 (and_3_out, not_4_out, D);
  not not_5 (not_5_out, A);
  and and_4 (and_4_out, not_5_out, B);
  and and_5 (and_5_out, A, not_6_out);
  not not_6 (not_6_out, B);
  or or_1 (Y7, and_1_out, and_2_out, and_3_out, and_4_out, and_5_out);
endmodule
