// Logisim project 7 segment display.circ as structural Verilog: 2 circuits, main circuit 0 number
module main (
  input  A,
  input  B,
  input  C,
  input  D,
  input  [3:0] ABCD
);

  wire n0_number_1_down, n0_number_1_left_down, n0_number_1_left_up, n0_number_1_middle,
       n0_number_1_right_down, n0_number_1_right_up, n0_number_1_up, nand_1_out, nand_2_out, nand_3_out,
       nand_4_out, nand_5_out, nand_6_out;

  nand nand_1 (nand_1_out, A, B, C, D);
  nand nand_2 (nand_2_out, A, B, C, D);
  nand nand_3 (nand_3_out, A, B, C, D);
  nand nand_4 (nand_4_out, A, B, C, D);
  nand nand_5 (nand_5_out, A, B, C, D);
  nand nand_6 (nand_6_out, A, B, C, D);
  _0_number u_0_number_1 (
    .in_1(ABCD), .Middle(n0_number_1_middle), .Left_Up(n0_number_1_left_up), .Up(n0_number_1_up),
    .Right_Up(n0_number_1_right_up), .Left_Down(n0_number_1_left_down), .Down(n0_number_1_down),
    .Right_Down(n0_number_1_right_down));
  _7_Segment_Display u_7_segment_display_1 (
    .g(n0_number_1_middle), .f(n0_number_1_left_up), .a(n0_number_1_up), .b(n0_number_1_right_up),
    .e(n0_number_1_left_down), .d(n0_number_1_down), .c(n0_number_1_right_down));  // open: dp
  _7_Segment_Display u_7_segment_display_2 (
    .f(nand_2_out), .a(nand_1_out), .b(nand_6_out), .e(nand_3_out), .d(nand_4_out), .c(nand_5_out));  // open: g, dp
endmodule

module _0_number (
  input  [3:0] in_1,
  output Middle,
  output Left_Up,
  output Up,
  output Right_Up,
  output Left_Down,
  output Down,
  output Right_Down
);

  nand nand_1 (Down, in_1[0], in_1[1], in_1[2], in_1[3]);
  not not_1 (Middle, Down);

  assign Left_Down = Down;
  assign Left_Up = Down;
  assign Right_Down = Down;
  assign Right_Up = Down;
  assign Up = Down;
endmodule
