// Logisim project 7digit.circ as structural Verilog: 6 circuits, main circuit Y1
module main (
  input  A,
  input  B,
  input  C,
  input  D,
  input  in_5,
  input  a_2,
  input  b_2,
  input  c_2,
  input  d_2
);

  wire and_1_out, and_2_out, and_3_out, and_4_out, and_5_out, and_6_out, not_1_out, not_2_out, not_3_out,
       not_4_out, or_1_out, undriven, y1_1_y1, y2_1_y2, y3_1_y3;

  not not_1 (not_1_out, A);
  not not_2 (not_2_out, D);
  not not_3 (not_3_out, B);
  not not_4 (not_4_out, C);
  and and_1 (and_1_out, not_1_out, C);
  and and_2 (and_2_out, C, B);
  and and_3 (and_3_out, not_2_out, A);
  and and_4 (and_4_out, not_1_out, B, D);
  and and_5 (and_5_out, not_3_out, not_4_out, A);
  and and_6 (and_6_out, not_2_out, not_3_out, not_4_out);
  or or_1 (or_1_out, and_1_out, and_3_out, and_2_out, and_4_out, and_5_out, and_6_out);
  Y3 y3_1 (.y3(y3_1_y3));  // open: a, b, c, d
  Y2 y2_1 (.y2(y2_1_y2));  // open: a, b, c, d
  Y1 y1_1 (.y1(y1_1_y1));  // open: a, b, c, d
  _7_Segment_Display u_7_segment_display_1 (.g(y1_1_y1), .f(y2_1_y2), .a(y3_1_y3));  // open: b, e, d, c, dp
  _7_Segment_Display u_7_segment_display_2 (.g(A), .f(A), .a(or_1_out), .d(undriven));  // open: b, e, c, dp
endmodule

module Y1 (
  input  a,
  input  b,
  input  c,
  input  d,
  output y1
);

  wire and_1_out, and_2_out, and_3_out, and_4_out, and_5_out, not_1_out, not_2_out, not_3_out, not_4_out,
       not_5_out;

  not not_1 (not_1_out, b);
  and and_1 (and_1_out, not_1_out, c);
  not not_2 (not_2_out, a);
  and and_2 (and_2_out, not_2_out, b, not_3_out);
  not not_3 (not_3_out, c);
  and and_3 (and_3_out, b, not_4_out);
  not not_4 (not_4_out, d);
  and and_4 (and_4_out, a, not_5_out);
  not not_5 (not_5_out, b);
  and and_5 (and_5_out, a, c);
  or or_1 (y1, and_1_out, and_2_out, and_3_out, and_4_out, and_5_out);
endmodule

module Y2 (
  input  a,
  input  b,
  input  c,
  input  d,
  output y2
);

  wire and_1_out, and_2_out, and_3_out, not_1_out, not_2_out, not_3_out, not_4_out;

  not not_1 (not_1_out, c);
  and and_1 (and_1_out, not_1_out, not_2_out);
  not not_2 (not_2_out, d);
  and and_2 (and_2_out, b, not_3_out);
  not not_3 (not_3_out, c);
  and and_3 (and_3_out, b, not_4_out);
  not not_4 (not_4_out, d);
  or or_1 (y2, and_1_out, and_2_out, and_3_out, a);
endmodule

module Y3 (
  input  a,
  input  b,
  input  c,
  input  d,
  output y3
);

  wire and_1_out, and_2_out, not_1_out, not_2_out;

  not not_1 (not_1_out, b);
  and and_1 (and_1_out, not_1_out, not_2_out);
  not not_2 (not_2_out, d);
  and and_2 (and_2_out, b, d);
  or or_1 (y3, and_1_out, c, and_2_out, a);
endmodule

// y4
module Y4 (
  input  a,
  input  b,
  input  c,
  input  d,
  output out_5
);

  wire and_1_out, and_2_out, and_3_out, not_1_out, not_2_out, not_3_out, not_4_out, not_5_out, not_6_out;

  not not_1 (not_1_out, a);
  and and_1 (and_1_out, not_1_out, not_2_out, not_3_out);
  not not_2 (not_2_out, c);
  not not_3 (not_3_out, d);
  not not_4 (not_4_out, b);
  not not_5 (not_5_out, a);
  and and_2 (and_2_out, not_5_out, c, d);
  and and_3 (and_3_out, a, not_6_out, d);
  not not_6 (not_6_out, c);
  or or_1 (out_5, and_1_out, not_4_out, and_2_out, and_3_out);
endmodule

module Y5 (
  input  a,
  input  b,
  input  c,
  input  d,
  output y5
);

  wire and_1_out, and_2_out, and_3_out, and_4_out, not_1_out, not_2_out, not_3_out;

  not not_1 (not_1_out, b);
  and and_1 (and_1_out, not_1_out, not_2_out);
  not not_2 (not_2_out, d);
  and and_2 (and_2_out, c, not_3_out);
  not not_3 (not_3_out, d);
  and and_3 (and_3_out, a, c);
  and and_4 (and_4_out, a, b);
  or or_1 (y5, and_1_out, and_2_out, and_3_out, and_4_out);
endmodule
